// Logisim project index.circ as structural Verilog: 6 circuits, main circuit main
module main (
  input  Clear,
  input  in_2,
  input  in_3,
  input  Binvert
);

  wire A_out, and_1_out, B_out, Clock__15_Cliques_out, mux_1_output, or_1_out, somador_1_output, xor_1_out,
       xor_2_out;
  wire [3:0] A_q3, A_q7, B_q3, B_q7;

  Clock Clock__15_Cliques (.out(Clock__15_Cliques_out));
  Shift_Register A (
    .in(mux_1_output), .clk(Clock__15_Cliques_out), .out(A_out), .clr(Clear), .q0(A_q3[3]), .q1(A_q3[2]),
    .q2(A_q3[1]), .q3(A_q3[0]), .q4(A_q7[3]), .q5(A_q7[2]), .q6(A_q7[1]), .q7(A_q7[0]));  // open: shift, load, d0, d1, d2, d3, d4, d5, d6, d7
  Shift_Register B (
    .in(1'b0), .clk(Clock__15_Cliques_out), .out(B_out), .q0(B_q3[3]), .q1(B_q3[2]), .q2(B_q3[1]),
    .q3(B_q3[0]), .q4(B_q7[3]), .q5(B_q7[2]), .q6(B_q7[1]), .q7(B_q7[0]));  // open: shift, load, clr, d0, d1, d2, d3, d4, d5, d6, d7
  Hex_Digit_Display hex_digit_display_1 (.value(A_q3));  // open: dp
  xor xor_1 (xor_1_out, B_out, Binvert);
  Hex_Digit_Display hex_digit_display_2 (.value(A_q7));  // open: dp
  Hex_Digit_Display hex_digit_display_3 (.value(B_q3));  // open: dp
  Hex_Digit_Display hex_digit_display_4 (.value(B_q7));  // open: dp
  and and_1 (and_1_out, A_out, B_out);
  or or_1 (or_1_out, A_out, B_out);
  xor xor_2 (xor_2_out, A_out, B_out);
  somador somador_1 (.A(A_out), .B(xor_1_out), .Clock(Clock__15_Cliques_out), .Output(somador_1_output));
  mux mux_1 (
    .S0(in_2), .S1(in_3), .D0(and_1_out), .D1(or_1_out), .D2(xor_2_out), .D3(somador_1_output),
    .Output(mux_1_output));
endmodule

// A
module registrador (
  input  Clock,
  input  C_In,
  input  in_3,
  input  in_4,
  input  in_5,
  input  in_6,
  input  in_7,
  input  in_8,
  input  in_9,
  input  in_10,
  input  Clear,
  output Q0,
  output Q1,
  output Q2,
  output Q3,
  output Q4,
  output Q5,
  output Q6,
  output Q7,
  output Q
);

  D_Flip_Flop d_ff_1 (.clk(Clock), .D(C_In), .Q(Q0), .preset(in_3), .reset(Clear));  // open: Qn, en
  D_Flip_Flop d_ff_2 (.clk(Clock), .D(Q0), .Q(Q1), .preset(in_4), .reset(Clear));  // open: Qn, en
  D_Flip_Flop d_ff_3 (.clk(Clock), .D(Q1), .Q(Q2), .preset(in_5), .reset(Clear));  // open: Qn, en
  D_Flip_Flop d_ff_4 (.clk(Clock), .D(Q2), .Q(Q3), .preset(in_6), .reset(Clear));  // open: Qn, en
  D_Flip_Flop d_ff_5 (.clk(Clock), .D(Q4), .Q(Q5), .preset(in_8), .reset(Clear));  // open: Qn, en
  D_Flip_Flop d_ff_6 (.clk(Clock), .D(Q3), .Q(Q4), .preset(in_7), .reset(Clear));  // open: Qn, en
  D_Flip_Flop d_ff_7 (.clk(Clock), .D(Q5), .Q(Q6), .preset(in_9), .reset(Clear));  // open: Qn, en
  D_Flip_Flop d_ff_8 (.clk(Clock), .D(Q6), .Q(Q), .preset(in_10), .reset(Clear));  // open: Qn, en

  assign Q7 = Q;
endmodule

// MUX
module mux (
  input  S0,
  input  S1,
  input  D0,
  input  D1,
  input  D2,
  input  D3,
  output Output
);

  wire and_1_out, and_2_out, and_3_out, and_4_out, not_1_out, not_2_out;

  not not_1 (not_1_out, S1);
  not not_2 (not_2_out, S0);
  and and_1 (and_1_out, not_1_out, D0, not_2_out);
  and and_2 (and_2_out, not_1_out, D1, S0);
  and and_3 (and_3_out, S1, D2, not_2_out);
  and and_4 (and_4_out, S1, D3, S0);
  or or_1 (Output, and_1_out, and_2_out, and_3_out, and_4_out);
endmodule

module base (
  input  clear,
  input  Binvert,
  input  [1:0] \Operação 
);

  wire A_out, adder_1_cout, adder_1_out, and_1_out, B_out, Carry_q, clock_1_out, multiplexer_1_out, or_1_out,
       xor_1_out, xor_2_out;
  wire [3:0] A_q3, A_q7, B_q3, B_q7;

  Clock clock_1 (.out(clock_1_out));
  Shift_Register B (
    .in(1'b0), .clk(clock_1_out), .out(B_out), .q0(B_q3[3]), .q1(B_q3[2]), .q2(B_q3[1]), .q3(B_q3[0]),
    .q4(B_q7[3]), .q5(B_q7[2]), .q6(B_q7[1]), .q7(B_q7[0]));  // open: shift, load, clr, d0, d1, d2, d3, d4, d5, d6, d7
  Shift_Register A (
    .in(multiplexer_1_out), .clk(clock_1_out), .out(A_out), .clr(clear), .q0(A_q3[3]), .q1(A_q3[2]),
    .q2(A_q3[1]), .q3(A_q3[0]), .q4(A_q7[3]), .q5(A_q7[2]), .q6(A_q7[1]), .q7(A_q7[0]));  // open: shift, load, d0, d1, d2, d3, d4, d5, d6, d7
  xor xor_1 (xor_1_out, B_out, Binvert);
  Hex_Digit_Display hex_digit_display_1 (.value(A_q7));  // open: dp
  Hex_Digit_Display hex_digit_display_2 (.value(A_q3));  // open: dp
  and and_1 (and_1_out, A_out, B_out);
  or or_1 (or_1_out, A_out, B_out);
  xor xor_2 (xor_2_out, A_out, B_out);
  Hex_Digit_Display hex_digit_display_3 (.value(B_q3));  // open: dp
  Hex_Digit_Display hex_digit_display_4 (.value(B_q7));  // open: dp
  Adder #(.width(1)) adder_1 (.a(A_out), .b(xor_1_out), .out(adder_1_out), .cin(Carry_q), .cout(adder_1_cout));
  D_Flip_Flop Carry (.clk(clock_1_out), .D(adder_1_cout), .Q(Carry_q));  // open: Qn, preset, en, reset
  Multiplexer #(.select(2), .enable("false")) multiplexer_1 (
    .in0(and_1_out), .in1(or_1_out), .in2(xor_2_out), .in3(adder_1_out), .out(multiplexer_1_out),
    .sel(\Operação ));
endmodule

module teste (
  input  Clear,
  input  in_2,
  input  in_3,
  input  Binvert
);

  wire A_out, and_1_out, B_out, Clock__15_Cliques_out, mux_1_output, or_1_out, somador_1_output, xor_1_out,
       xor_2_out;
  wire [3:0] A_q3, A_q7, B_q3, B_q7;

  Shift_Register B (
    .in(1'b0), .clk(Clock__15_Cliques_out), .out(B_out), .q0(B_q3[3]), .q1(B_q3[2]), .q2(B_q3[1]),
    .q3(B_q3[0]), .q4(B_q7[3]), .q5(B_q7[2]), .q6(B_q7[1]), .q7(B_q7[0]));  // open: shift, load, clr, d0, d1, d2, d3, d4, d5, d6, d7
  Clock Clock__15_Cliques (.out(Clock__15_Cliques_out));
  Shift_Register A (
    .in(mux_1_output), .clk(Clock__15_Cliques_out), .out(A_out), .clr(Clear), .q0(A_q3[3]), .q1(A_q3[2]),
    .q2(A_q3[1]), .q3(A_q3[0]), .q4(A_q7[3]), .q5(A_q7[2]), .q6(A_q7[1]), .q7(A_q7[0]));  // open: shift, load, d0, d1, d2, d3, d4, d5, d6, d7
  xor xor_1 (xor_1_out, B_out, Binvert);
  Hex_Digit_Display hex_digit_display_1 (.value(A_q3));  // open: dp
  Hex_Digit_Display hex_digit_display_2 (.value(A_q7));  // open: dp
  and and_1 (and_1_out, A_out, B_out);
  or or_1 (or_1_out, A_out, B_out);
  xor xor_2 (xor_2_out, A_out, B_out);
  Hex_Digit_Display hex_digit_display_3 (.value(B_q7));  // open: dp
  Hex_Digit_Display hex_digit_display_4 (.value(B_q3));  // open: dp
  somador somador_1 (.A(A_out), .B(xor_1_out), .Clock(Clock__15_Cliques_out), .Output(somador_1_output));
  mux mux_1 (
    .S0(in_2), .S1(in_3), .D0(and_1_out), .D1(or_1_out), .D2(xor_2_out), .D3(somador_1_output),
    .Output(mux_1_output));
endmodule

// FA
module somador (
  input  A,
  input  B,
  input  Clock,
  output Output
);

  wire and_1_out, and_2_out, d_ff_1_q, or_1_out, xor_1_out;

  D_Flip_Flop d_ff_1 (.clk(Clock), .D(or_1_out), .Q(d_ff_1_q));  // open: Qn, preset, en, reset
  xor xor_1 (xor_1_out, A, B);
  and and_1 (and_1_out, A, B);
  and and_2 (and_2_out, d_ff_1_q, xor_1_out);
  xor xor_2 (Output, xor_1_out, d_ff_1_q);
  or or_1 (or_1_out, and_2_out, and_1_out);
endmodule
